# Fritzing sketch 3DMapControl (saved by Fritzing 0.5.2b)

parts:
  Arduino1 = Arduino
  J1 = female pin header, 4 pins [form="♂ (male)"]

nets:
  N1: Arduino1.GND, J1.pin4
  N2: Arduino1.3V3, J1.pin3
  N3: Arduino1.A4, J1.pin2
  N4: Arduino1.A5, J1.pin1

notes:
  Header reperesents Wii Nunchuk connector / matches pinout for WiiChuck adapter
