# Fritzing sketch easyProgramLauncher (saved by Fritzing 0.5.2b)
breadboards: 1

parts:
  Teensy1 = Teensy 2.0
  S1 = Pushbutton [package="[THT]"]
  S2 = Toggle Switch [package=THT]

nets:
  N1: Teensy1.GND, S1.Pin_1, S1.Pin_2, S2.COM
  N2: Teensy1.B0, S1.Pin_3, S1.Pin_4
  N3: Teensy1.B1, S2.L1
