# Fritzing sketch mailboxMonitor (saved by Fritzing 0.5.2b)
breadboards: 1

parts:
  Arduino1 = Arduino
  LED2 = white LED - 5mm [package="5 mm [THT]"]
  LED1 = Blue LED - 5mm [package="5 mm [THT]"]
  R1 = Resistor [resistance=100k package=THT]
  R2 = Resistor [resistance=100 package=THT]
  J1 = female pin header, 4 pins [form="♀ (female)"]

nets:
  N1: Arduino1.GND, LED2.anode, LED1.cathode, J1.pin1
  N2: Arduino1.D9, R2.Pin_0
  N3: Arduino1.D8, R1.Pin_1
  N4: Arduino1.D3, LED2.cathode, R1.Pin_0
  N5: Arduino1.D1TX, J1.pin4
  N6: Arduino1.D0RX, J1.pin3
  N7: Arduino1.+5V, J1.pin2
  N8: LED1.anode, R2.Pin_1

notes:
  Photo transistor
  IR emitter
  XBee Explorer breakout board from Sparkfun
