# Fritzing sketch ringtoneJukebox (saved by Fritzing 0.5.2b)
breadboards: 1

parts:
  Arduino1 = Arduino
  S1 = Pushbutton [package="[THT]"]
  S2 = Pushbutton [package="[THT]"]
  S3 = Pushbutton [package="[THT]"]
  R1 = Resistor [resistance=10k package=THT]
  R2 = Resistor [resistance=10k package=THT]
  R3 = Resistor [resistance=10k package=THT]
  LED1 = Red LED - 5mm [package="5 mm [THT]"]
  R4 = Resistor [resistance=330 package=THT]
  J1 = Piezo Speaker
  R5 = Resistor [resistance=100 package=THT]

nets:
  N1: Arduino1.GND, R1.Pin_0, R2.Pin_0, R3.Pin_0, LED1.cathode, J1.pin1
  N2: Arduino1.D12, R4.Pin_0
  N3: Arduino1.D8, R5.Pin_0
  N4: Arduino1.D7, S2.Pin_1, S2.Pin_2, R2.Pin_1
  N5: Arduino1.D6, S3.Pin_1, S3.Pin_2, R3.Pin_1
  N6: Arduino1.D5, S1.Pin_1, S1.Pin_2, R1.Pin_1
  N7: Arduino1.+5V, S1.Pin_3, S1.Pin_4, S2.Pin_3, S2.Pin_4, S3.Pin_3, S3.Pin_4
  N8: LED1.anode, R4.Pin_1
  N9: J1.pin2, R5.Pin_1
